// Digital circuit 2_Demux_1to4.dig as structural Verilog
module _2_Demux_1to4 (
  input  Data,
  input  Sel1,
  input  Sel0,
  output Out0,
  output Out1,
  output Out2,
  output Out3
);

  wire ip0, ip1;

  not not_1 (ip0, Sel0);
  not not_2 (ip1, Sel1);
  and and_1 (Out0, Data, ip0, ip1);
  and and_2 (Out1, Data, Sel0, ip1);
  and and_3 (Out2, Data, ip0, Sel1);
  and and_4 (Out3, Data, Sel0, Sel1);

  // Other names for the same wires on the sheet: D = Data; i0 = Sel0; i1 = Sel1
endmodule
