// Digital circuit 3a_SR_flip_flop.dig as structural Verilog
module _3a_SR_flip_flop (
  input  S,
  input  C,
  input  R,
  output Q,
  output Q_2
);

  wire nand_1_out, nand_2_out, nand_3_out, nand_4_out, nand_5_out, nand_6_out, not_1_out;

  nand nand_1 (nand_1_out, S, C);
  nand nand_2 (nand_2_out, C, R);
  not not_1 (not_1_out, C);
  nand nand_3 (nand_3_out, nand_1_out, nand_4_out);
  nand nand_4 (nand_4_out, nand_3_out, nand_2_out);
  nand nand_5 (nand_5_out, nand_3_out, not_1_out);
  nand nand_6 (nand_6_out, not_1_out, nand_4_out);
  nand nand_7 (Q, nand_5_out, Q_2);
  nand nand_8 (Q_2, Q, nand_6_out);

  // Notes on the sheet:
  //   Master-Slave SR
  //   En esta conexión entre flip flops, permite el control
  //   y permanencia de un dato durante un ciclo entero, 
  //   en este diseño al realizar un ciclo con set y reset 
  //   encendidos, causa un corto en el output final al
  //   cerrar el ciclo.
endmodule
