// Digital circuit 3b_JK_flip_flop.dig as structural Verilog
module _3b_JK_flip_flop (
  input  S,
  input  C,
  input  R,
  output Q,
  output Q_2
);

  wire nand_1_out, nand_2_out, nand_3_out, nand_4_out, nand_5_out, nand_6_out, not_1_out;

  nand nand_1 (nand_1_out, Q_2, S, C);
  nand nand_2 (nand_2_out, C, R, Q);
  not not_1 (not_1_out, C);
  nand nand_3 (nand_3_out, nand_1_out, nand_4_out);
  nand nand_4 (nand_4_out, nand_3_out, nand_2_out);
  nand nand_5 (nand_5_out, nand_3_out, not_1_out);
  nand nand_6 (nand_6_out, not_1_out, nand_4_out);
  nand nand_7 (Q, nand_5_out, Q_2);
  nand nand_8 (Q_2, Q, nand_6_out);

  // Notes on the sheet:
  //   Master-Slave JK 
  //   En esta conexión entre flip flops, permite el control
  //   y permanencia de un dato durante un ciclo entero, 
  //   en este diseño no sucede la oscilación del flip flop 
  //   SR, por la interacción de las salidas con las entradas, 
  //   permite una oscilación controlada de los datos.
endmodule
