// Digital circuit 4_Pin_I_O_v2.dig as structural Verilog
module _4_Pin_I_O_v2 (
  input  Set,
  input  C3,
  input  C2,
  input  C1,
  input  C0,
  input  Clear,
  input  Clock,
  input  in_9,
  input  in_11,
  input  in_13,
  input  in_15,
  input  Set_2,
  input  Clear_2,
  input  Clock_2,
  input  Set_3,
  input  S3,
  input  S2,
  input  S1,
  input  S0,
  input  Clear_3,
  input  Clock_3,
  input  Enable,
  output out_8,
  output out_10,
  output out_12,
  output out_14,
  output out_19,
  output out_20,
  output out_21,
  output out_22
);

  wire d_ff_as_5_q, d_ff_as_6_q, d_ff_as_7_q, d_ff_as_8_q, e0, e1, e2, e3, multiplexer_1_out,
       multiplexer_2_out, multiplexer_3_out, multiplexer_4_out, s0_t, s1_t, s2_t, s3_t;

  D_FF_AS d_ff_as_1 (.Set(Set_3), .D(S3), .C(Clock_3), .Clr(Clear_3), .Q(s3_t));  // open: nQ
  D_FF_AS d_ff_as_2 (.Set(Set_3), .D(S2), .C(Clock_3), .Clr(Clear_3), .Q(s2_t));  // open: nQ
  D_FF_AS d_ff_as_3 (.Set(Set_3), .D(S1), .C(Clock_3), .Clr(Clear_3), .Q(s1_t));  // open: nQ
  D_FF_AS d_ff_as_4 (.Set(Set_3), .D(S0), .C(Clock_3), .Clr(Clear_3), .Q(s0_t));  // open: nQ
  D_FF_AS d_ff_as_5 (.Set(Set), .D(C3), .C(Clock), .Clr(Clear), .Q(d_ff_as_5_q));  // open: nQ
  assign out_14 = ~d_ff_as_5_q ? s3_t : 1'bz;  // DriverInvSel driverinvsel_1
  D_FF_AS d_ff_as_6 (.Set(Set), .D(C2), .C(Clock), .Clr(Clear), .Q(d_ff_as_6_q));  // open: nQ
  assign e3 = d_ff_as_5_q ? in_15 : 1'bz;  // Driver driver_1
  assign out_12 = ~d_ff_as_6_q ? s2_t : 1'bz;  // DriverInvSel driverinvsel_2
  assign e2 = d_ff_as_6_q ? in_13 : 1'bz;  // Driver driver_2
  D_FF_AS d_ff_as_7 (.Set(Set), .D(C1), .C(Clock), .Clr(Clear), .Q(d_ff_as_7_q));  // open: nQ
  assign out_10 = ~d_ff_as_7_q ? s1_t : 1'bz;  // DriverInvSel driverinvsel_3
  assign e1 = d_ff_as_7_q ? in_11 : 1'bz;  // Driver driver_3
  D_FF_AS d_ff_as_8 (.Set(Set), .D(C0), .C(Clock), .Clr(Clear), .Q(d_ff_as_8_q));  // open: nQ
  assign out_8 = ~d_ff_as_8_q ? s0_t : 1'bz;  // DriverInvSel driverinvsel_4
  assign e0 = d_ff_as_8_q ? in_9 : 1'bz;  // Driver driver_4
  PullDown pulldown_1 (.out(e3));
  Multiplexer multiplexer_1 (.sel(Enable), .in_0(out_19), .in_1(e3), .out(multiplexer_1_out));
  D_FF_AS d_ff_as_9 (.Set(Set_2), .D(multiplexer_1_out), .C(Clock_2), .Clr(Clear_2), .Q(out_19));  // open: nQ
  PullDown pulldown_2 (.out(e2));
  Multiplexer multiplexer_2 (.sel(Enable), .in_0(out_20), .in_1(e2), .out(multiplexer_2_out));
  D_FF_AS d_ff_as_10 (.Set(Set_2), .D(multiplexer_2_out), .C(Clock_2), .Clr(Clear_2), .Q(out_20));  // open: nQ
  PullDown pulldown_3 (.out(e1));
  Multiplexer multiplexer_3 (.sel(Enable), .in_0(out_21), .in_1(e1), .out(multiplexer_3_out));
  D_FF_AS d_ff_as_11 (.Set(Set_2), .D(multiplexer_3_out), .C(Clock_2), .Clr(Clear_2), .Q(out_21));  // open: nQ
  PullDown pulldown_4 (.out(e0));
  Multiplexer multiplexer_4 (.sel(Enable), .in_0(out_22), .in_1(e0), .out(multiplexer_4_out));
  D_FF_AS d_ff_as_12 (.Set(Set_2), .D(multiplexer_4_out), .C(Clock_2), .Clr(Clear_2), .Q(out_22));  // open: nQ

  // Notes on the sheet:
  //   Clock: Hz: 2
  //   Clock_2: Hz: 2
  //   Clock_3: Hz: 2
  //   Registro entrega a salida
  //   Determina los datos a enviar para salida.
  //   Registro configuración
  //   Selecciona si enviar el dato al 
  //   almacenamiento o salida.
  //   Registro almacenamiento
  //   Recibe el dato del pin respectivo para
  //   su guardado.
endmodule
