// Digital circuit Multiplexer_8entries.dig as structural Verilog
module Multiplexer_8entries (
  input  D0,
  input  D1,
  input  D2,
  input  D3,
  input  D4,
  input  D5,
  input  D6,
  input  D7,
  input  Sel2,
  input  Sel1,
  input  Sel0,
  output out_1
);

  wire and_1_out, and_2_out, and_3_out, and_4_out, and_5_out, and_6_out, and_7_out, and_8_out, ip0, ip1, ip2,
       or_1_out, or_2_out;

  not not_1 (ip2, Sel2);
  not not_2 (ip1, Sel1);
  not not_3 (ip0, Sel0);
  and and_1 (and_1_out, D0, ip0, ip1, ip2);
  and and_2 (and_2_out, D1, Sel0, ip1, ip2);
  and and_3 (and_3_out, D2, ip0, Sel1, ip2);
  and and_4 (and_4_out, D3, Sel0, Sel1, ip2);
  and and_5 (and_5_out, D4, ip0, ip1, Sel2);
  and and_6 (and_6_out, D5, Sel0, ip1, Sel2);
  and and_7 (and_7_out, D6, ip0, Sel1, Sel2);
  and and_8 (and_8_out, D7, Sel0, Sel1, Sel2);
  or or_1 (or_1_out, and_1_out, and_2_out, and_3_out, and_4_out);
  or or_2 (or_2_out, and_5_out, and_6_out, and_7_out, and_8_out);
  or or_3 (out_1, or_1_out, or_2_out);

  // Other names for the same wires on the sheet: i0 = Sel0; i1 = Sel1; i2 = Sel2
endmodule
