// Digital circuit Pines I_O.dig as structural Verilog
module Pines_I_O (
  input  Set,
  input  C3,
  input  C2,
  input  C1,
  input  C0,
  input  Clear,
  input  Clock,
  input  Set_2,
  input  Clear_2,
  input  Set_3,
  input  Clear_3,
  input  D3,
  input  D2,
  input  D1,
  input  D0,
  input  in_25,
  output out_8,
  output out_11,
  output out_12,
  output out_13,
  output out_14,
  output out_21,
  output out_22,
  output out_23,
  output out_24
);

  wire c0_t, c1_t, c2_t, c3_t, cn0, cn1, cn2, cn3, d_ff_as_5_q, d_ff_as_7_q, d_ff_as_8_q, d_ff_as_10_q,
       driver_2_out, driver_3_out, driver_5_out, driver_7_out, driver_9_out, undriven, undriven_2;

  D_FF_AS d_ff_as_1 (.Set(Set), .D(C0), .C(Clock), .Clr(Clear), .Q(c0_t));  // open: nQ
  D_FF_AS d_ff_as_2 (.Set(Set), .D(C1), .C(Clock), .Clr(Clear), .Q(c1_t));  // open: nQ
  D_FF_AS d_ff_as_3 (.Set(Set), .D(C2), .C(Clock), .Clr(Clear), .Q(c2_t));  // open: nQ
  D_FF_AS d_ff_as_4 (.Set(Set), .D(C3), .C(Clock), .Clr(Clear), .Q(c3_t));  // open: nQ
  not not_1 (cn0, c0_t);
  not not_2 (cn1, c1_t);
  not not_3 (cn2, c2_t);
  not not_4 (cn3, c3_t);
  D_FF_AS d_ff_as_5 (.Set(Set_3), .D(D3), .C(Clock), .Clr(Clear_3), .Q(d_ff_as_5_q));  // open: nQ
  assign out_8 = cn3 ? d_ff_as_5_q : 1'bz;  // Driver driver_1
  assign driver_2_out = c3_t ? Clock : 1'bz;  // Driver driver_2
  assign driver_3_out = undriven_2 ? in_25 : 1'bz;  // Driver driver_3
  assign out_24 = ~undriven_2 ? undriven : 1'bz;  // DriverInvSel driverinvsel_1
  D_FF_AS d_ff_as_6 (.Set(Set_2), .D(d_ff_as_5_q), .C(driver_2_out), .Clr(Clear_2), .Q(out_11));  // open: nQ
  D_FF_AS d_ff_as_7 (.Set(Set_3), .D(D2), .C(Clock), .Clr(Clear_3), .Q(d_ff_as_7_q));  // open: nQ
  assign out_21 = cn2 ? d_ff_as_7_q : 1'bz;  // Driver driver_4
  assign driver_5_out = c2_t ? Clock : 1'bz;  // Driver driver_5
  D_FF_AS d_ff_as_8 (.Set(Set_3), .D(D1), .C(Clock), .Clr(Clear_3), .Q(d_ff_as_8_q));  // open: nQ
  D_FF_AS d_ff_as_9 (.Set(Set_2), .D(d_ff_as_7_q), .C(driver_5_out), .Clr(Clear_2), .Q(out_12));  // open: nQ
  assign out_22 = cn1 ? d_ff_as_8_q : 1'bz;  // Driver driver_6
  D_FF_AS d_ff_as_10 (.Set(Set_3), .D(D0), .C(Clock), .Clr(Clear_3), .Q(d_ff_as_10_q));  // open: nQ
  D_FF_AS d_ff_as_11 (.Set(Set_2), .D(d_ff_as_8_q), .C(driver_7_out), .Clr(Clear_2), .Q(out_13));  // open: nQ
  assign driver_7_out = c1_t ? Clock : 1'bz;  // Driver driver_7
  assign out_23 = cn0 ? d_ff_as_10_q : 1'bz;  // Driver driver_8
  assign driver_9_out = c0_t ? Clock : 1'bz;  // Driver driver_9
  D_FF_AS d_ff_as_12 (.Set(Set_2), .D(d_ff_as_10_q), .C(driver_9_out), .Clr(Clear_2), .Q(out_14));  // open: nQ

  // Other names for the same wires on the sheet: cl = Clock

  // Notes on the sheet:
  //   Clock: Hz: 2
  //   Registro configuración
  //   Selecciona si enviar el dato al 
  //   almacenamiento o salida.
  //   Registro Pines
  //   Permite la recepción de información
  //   para guardado o salida.
  //   Registro almacenamiento
  //   Registro almacenamiento
  //   Guarda la información del dato.
endmodule
